// Logisim project Nourin_Lab_5.circ as structural Verilog
module R_Type (
  input  [15:0] in_1,
  input  Write_EN,
  output [3:0] Write_REG,
  output [3:0] Read_REG01,
  output [3:0] Read_REG02,
  output [3:0] OP_Code,
  output [15:0] out_7,
  output [15:0] out_8
);

  wire CLK_out;
  wire [15:0] adder_1_out, undriven;

  Clock CLK (.out(CLK_out));
  Adder #(.width(16)) adder_1 (.a(undriven), .b(16'h1), .out(adder_1_out));  // open: cin, cout
  Register #(.width(16)) register_1 (.D(undriven), .Q(adder_1_out), .clk(CLK_out));  // open: en, clr
  ROM #(.addrWidth(16), .dataWidth(16)) rom_1 (.addr(adder_1_out), .data({OP_Code, Read_REG02, Read_REG01, Write_REG}));
  Register_16Bit register_16bit_1 (
    .Read_REG_1(Read_REG01), .Read_REG_2(Read_REG02), .Data_Input(in_1), .Write_Reg(Write_REG),
    .write_Enable(Write_EN), .CLOCK(CLK_out), .Read_Data_1(out_7), .Read_data_2(out_8));

  // Notes on the sheet:
  //   contents of rom_1 (hex, n*v repeats v):
  //   126
endmodule

module Register_16Bit (
  input  [3:0] Read_REG_1,
  input  [3:0] Read_REG_2,
  input  [15:0] Data_Input,
  input  [3:0] Write_Reg,
  input  write_Enable,
  input  CLOCK,
  output [15:0] Read_Data_1,
  output [15:0] Read_data_2
);

  wire and_1_out, and_2_out, and_3_out, and_4_out, and_5_out, and_6_out, and_7_out, and_8_out, and_9_out,
       and_10_out, and_11_out, and_12_out, and_13_out, and_14_out, and_15_out, and_16_out, decoder_1_out0,
       decoder_1_out1, decoder_1_out2, decoder_1_out3, decoder_1_out4, decoder_1_out5, decoder_1_out6,
       decoder_1_out7, decoder_1_out8, decoder_1_out9, decoder_1_out10, decoder_1_out11, decoder_1_out12,
       decoder_1_out13, decoder_1_out14, decoder_1_out15;
  wire [15:0] R0_q, R2_q, R4_q, R5_q, register_1_q, register_2_q, register_3_q, register_4_q, register_5_q,
       register_6_q, register_7_q, register_8_q, register_9_q, register_10_q, register_11_q, register_12_q;

  Decoder #(.select(4)) decoder_1 (
    .out0(decoder_1_out0), .out1(decoder_1_out1), .out2(decoder_1_out2), .out3(decoder_1_out3),
    .out4(decoder_1_out4), .out5(decoder_1_out5), .out6(decoder_1_out6), .out7(decoder_1_out7),
    .out8(decoder_1_out8), .out9(decoder_1_out9), .out10(decoder_1_out10), .out11(decoder_1_out11),
    .out12(decoder_1_out12), .out13(decoder_1_out13), .out14(decoder_1_out14), .out15(decoder_1_out15),
    .sel(Write_Reg));  // open: en
  and and_1 (and_1_out, decoder_1_out0, write_Enable);
  and and_2 (and_2_out, decoder_1_out1, write_Enable);
  and and_3 (and_3_out, decoder_1_out2, write_Enable);
  and and_4 (and_4_out, decoder_1_out3, write_Enable);
  and and_5 (and_5_out, decoder_1_out4, write_Enable);
  and and_6 (and_6_out, decoder_1_out5, write_Enable);
  and and_7 (and_7_out, decoder_1_out6, write_Enable);
  and and_8 (and_8_out, decoder_1_out7, write_Enable);
  and and_9 (and_9_out, decoder_1_out8, write_Enable);
  and and_10 (and_10_out, decoder_1_out9, write_Enable);
  and and_11 (and_11_out, decoder_1_out10, write_Enable);
  and and_12 (and_12_out, decoder_1_out11, write_Enable);
  and and_13 (and_13_out, decoder_1_out12, write_Enable);
  and and_14 (and_14_out, decoder_1_out13, write_Enable);
  and and_15 (and_15_out, decoder_1_out14, write_Enable);
  and and_16 (and_16_out, decoder_1_out15, write_Enable);
  Register #(.width(16)) R0 (.D(Data_Input), .en(and_1_out), .Q(R0_q), .clk(CLOCK));  // open: clr
  Register #(.width(16)) R2 (.D(Data_Input), .en(and_2_out), .Q(R2_q), .clk(CLOCK));  // open: clr
  Register #(.width(16)) register_1 (.D(Data_Input), .en(and_3_out), .Q(register_1_q), .clk(CLOCK));  // open: clr
  Register #(.width(16)) R5 (.D(Data_Input), .en(and_4_out), .Q(R5_q), .clk(CLOCK));  // open: clr
  Register #(.width(16)) R4 (.D(Data_Input), .en(and_5_out), .Q(R4_q), .clk(CLOCK));  // open: clr
  Register #(.width(16)) register_2 (.D(Data_Input), .en(and_6_out), .Q(register_2_q), .clk(CLOCK));  // open: clr
  Register #(.width(16)) register_3 (.D(Data_Input), .en(and_7_out), .Q(register_3_q), .clk(CLOCK));  // open: clr
  Register #(.width(16)) register_4 (.D(Data_Input), .en(and_8_out), .Q(register_4_q), .clk(CLOCK));  // open: clr
  Register #(.width(16)) register_5 (.D(Data_Input), .en(and_9_out), .Q(register_5_q), .clk(CLOCK));  // open: clr
  Register #(.width(16)) register_6 (.D(Data_Input), .en(and_10_out), .Q(register_6_q), .clk(CLOCK));  // open: clr
  Register #(.width(16)) register_7 (.D(Data_Input), .en(and_11_out), .Q(register_7_q), .clk(CLOCK));  // open: clr
  Register #(.width(16)) register_8 (.D(Data_Input), .en(and_12_out), .Q(register_8_q), .clk(CLOCK));  // open: clr
  Register #(.width(16)) register_9 (.D(Data_Input), .en(and_13_out), .Q(register_9_q), .clk(CLOCK));  // open: clr
  Register #(.width(16)) register_10 (.D(Data_Input), .en(and_14_out), .Q(register_10_q), .clk(CLOCK));  // open: clr
  Register #(.width(16)) register_11 (.D(Data_Input), .en(and_15_out), .Q(register_11_q), .clk(CLOCK));  // open: clr
  Register #(.width(16)) register_12 (.D(Data_Input), .en(and_16_out), .Q(register_12_q), .clk(CLOCK));  // open: clr
  Multiplexer #(.select(4), .width(16)) multiplexer_1 (
    .in0(R0_q), .in1(R2_q), .in2(register_1_q), .in3(R5_q), .in4(R4_q), .in5(register_2_q),
    .in6(register_3_q), .in7(register_4_q), .in8(register_5_q), .in9(register_6_q), .in10(register_7_q),
    .in11(register_8_q), .in12(register_9_q), .in13(register_10_q), .in14(register_11_q),
    .in15(register_12_q), .out(Read_Data_1), .sel(Read_REG_1));
  Multiplexer #(.select(4), .width(16)) multiplexer_2 (
    .in0(R0_q), .in1(R2_q), .in2(register_1_q), .in3(R5_q), .in4(R4_q), .in5(register_2_q),
    .in6(register_3_q), .in7(register_4_q), .in8(register_5_q), .in9(register_6_q), .in10(register_7_q),
    .in11(register_8_q), .in12(register_9_q), .in13(register_10_q), .in14(register_11_q),
    .in15(register_12_q), .out(Read_data_2), .sel(Read_REG_2));
endmodule
